# Fritzing sketch HC-05 (saved by Fritzing 0.8.7b)
breadboards: 1

parts:
  Part1 = Arduino Board Ethernet
  Part2 = HC-05 [part_number=HC-05 package="breakout board"]
  J1 = Basic Servo

nets:
  N1: Part1.D0/RX, Part2.TXD
  N2: Part1.D1/TX, Part2.RXD
  N3: Part1.D7, J1.pulse
  VCC: Part1.5V, Part2.VCC, J1.vcc
  GND: Part1.GND, Part2.GND, J1.gnd

notes:
  shreenidhi

custom parts:
  HC-05: A commonly available HC-05 Bluetooth breakout board.
